// Logisim project arm_single_cycle.circ as structural Verilog: 27 circuits, main circuit main
module main (
  input  in_1,
  input  in_2,
  input  in_3,
  input  [1:0] Branch,
  input  in_5,
  input  in_6,
  input  in_7,
  input  in_8,
  input  in_9,
  input  in_10,
  input  in_11,
  input  in_12,
  input  in_13,
  input  in_14,
  input  in_15,
  input  in_16,
  input  in_17,
  input  in_18,
  input  in_19,
  input  [3:0] in_20,
  input  [3:0] in_21,
  input  [31:0] A,
  input  [31:0] B,
  input  [1:0] in_24,
  input  [3:0] in_25,
  output out_26,
  output out_27,
  output out_28,
  output out_29,
  output out_30,
  output out_31,
  output out_32,
  output out_33,
  output [3:0] out_34,
  output [31:0] out_35,
  output out_36,
  output out_37,
  output out_38,
  output out_39
);

  wire and_2_out, and_3_out;
  wire [31:0] rom_1_data;

  // Probe on A
  and and_1 (out_26, in_1, in_2);
  // Probe on B
  Decoder #(.select(4)) decoder_1 (
    .out0(out_27), .out1(out_28), .out2(out_29), .out3(out_30), .out4(out_31), .out5(out_32), .sel(in_20));  // open: out6, out7, out8, out9, out10, out11, out12, out13, out14, out15, en
  ALU_conditional alu_conditional_1 (
    .ALU_Control(in_24), .r(out_35), .Zero(out_38), .ALU_FLAGS(out_34), .Negative(out_37), .Carry(out_36),
    .Overflow(out_39), .A(A), .B(B));
  // Probe on out_35
  // Probe on Branch[1]
  Multiplexer #(.select(4)) multiplexer_1 (
    .in0(in_3), .in1(in_5), .in2(in_6), .in3(in_7), .in4(in_8), .in5(in_9), .in6(in_10), .in7(in_11),
    .in8(in_12), .in9(in_13), .in10(in_14), .in11(in_15), .in12(in_16), .in13(in_17), .in14(in_18),
    .in15(in_19), .out(out_33), .sel(in_21));  // open: en
  ROM #(.addrWidth(4), .dataWidth(32)) rom_1 (.addr(in_25), .data(rom_1_data));  // open: sel
  and and_2 (and_2_out, 1'b1, Branch[0]);
  buf and_3 (and_3_out, ~Branch[1]);  // AND_Gate AND_Gate
  // AND_Gate and_4 has open pins: in0=and_2_out, in1=and_3_out, out=open

  // Notes on the sheet:
  //   Check branch inst in PC logic using 2-bit input
endmodule

module ALU (
  input  [31:0] A,
  input  [31:0] B,
  input  [1:0] ALU_Control,
  output [31:0] r
);

  wire [31:0] adder_1_out, and_1_out, or_1_out, subtractor_1_out;

  // Probe on A
  // Probe on B
  Adder #(.width(32)) adder_1 (.a(A), .b(B), .out(adder_1_out));  // open: cin, cout
  Subtractor #(.width(32)) subtractor_1 (.a(A), .b(B), .out(subtractor_1_out));  // open: bin, bout
  assign or_1_out = A | B;  // OR_Gate or_1, 32 bits wide
  assign and_1_out = A & B;  // AND_Gate and_1, 32 bits wide
  Multiplexer #(.select(2), .width(32)) multiplexer_1 (
    .in0(adder_1_out), .in1(subtractor_1_out), .in2(or_1_out), .in3(and_1_out), .out(r), .sel(ALU_Control));  // open: en
  // Probe on r
endmodule

module data_memory (
  input  clk,
  input  we,
  input  RESET,
  input  [31:0] address,
  input  [31:0] wd,
  output [31:0] rd
);

  wire not_1_out;

  not not_1 (not_1_out, we);
  RAM #(.dataWidth(32), .bus("separate")) ram_1 (
    .addr(address[9:2]), .din(wd), .data(rd), .str(we), .sel(1'b1), .clk(clk), .ld(not_1_out), .clr(RESET));
endmodule

module instruction_memory (
  input  [31:0] addr,
  output [31:0] rd
);

  // Probe on addr
  ROM #(.dataWidth(32)) rom_1 (.addr(addr[9:2]), .data(rd), .sel(1'b1));
  // Probe on rd

  // Notes on the sheet:
  //   Extract word address
  //   contents of rom_1 (hex, n*v repeats v):
  //   e0800001 e12fff1e
endmodule

module register_file (
  input  [31:0] R15,
  input  we,
  input  [3:0] writeAddr,
  input  [31:0] writeData,
  input  clk,
  input  Reset,
  input  [3:0] A1,
  input  [3:0] A2,
  output [31:0] RD1,
  output [31:0] RD2
);

  wire decoder_1_out0, decoder_1_out1, decoder_1_out2, decoder_1_out3, decoder_1_out4, decoder_1_out5,
       decoder_1_out6, decoder_1_out7, decoder_1_out8, decoder_1_out9, decoder_1_out10, decoder_1_out11,
       decoder_1_out12, decoder_1_out13, decoder_1_out14;
  wire [31:0] R0_q, R1_q, R2_q, R3_q, R5_q, R6_q, R7_q, R8_q, R9_q, R10_q, R11_q, R12_q, R13_q, R14_q,
       register_1_q;

  Decoder #(.select(4)) decoder_1 (
    .out0(decoder_1_out0), .out1(decoder_1_out1), .out2(decoder_1_out2), .out3(decoder_1_out3),
    .out4(decoder_1_out4), .out5(decoder_1_out5), .out6(decoder_1_out6), .out7(decoder_1_out7),
    .out8(decoder_1_out8), .out9(decoder_1_out9), .out10(decoder_1_out10), .out11(decoder_1_out11),
    .out12(decoder_1_out12), .out13(decoder_1_out13), .out14(decoder_1_out14), .sel(writeAddr), .en(we));  // open: out15
  Register #(.width(32)) R0 (.D(writeData), .en(decoder_1_out0), .Q(R0_q), .clk(clk), .clr(Reset));
  Register #(.width(32)) R1 (.D(writeData), .en(decoder_1_out1), .Q(R1_q), .clk(clk), .clr(Reset));
  Register #(.width(32)) R2 (.D(writeData), .en(decoder_1_out2), .Q(R2_q), .clk(clk), .clr(Reset));
  Register #(.width(32)) R3 (.D(writeData), .en(decoder_1_out3), .Q(R3_q), .clk(clk), .clr(Reset));
  Register #(.width(32)) register_1 (.D(writeData), .en(decoder_1_out4), .Q(register_1_q), .clk(clk), .clr(Reset));
  Register #(.width(32)) R5 (.D(writeData), .en(decoder_1_out5), .Q(R5_q), .clk(clk), .clr(Reset));
  Register #(.width(32)) R6 (.D(writeData), .en(decoder_1_out6), .Q(R6_q), .clk(clk), .clr(Reset));
  Register #(.width(32)) R7 (.D(writeData), .en(decoder_1_out7), .Q(R7_q), .clk(clk), .clr(Reset));
  Register #(.width(32)) R8 (.D(writeData), .en(decoder_1_out8), .Q(R8_q), .clk(clk), .clr(Reset));
  Register #(.width(32)) R9 (.D(writeData), .en(decoder_1_out9), .Q(R9_q), .clk(clk), .clr(Reset));
  Register #(.width(32)) R10 (.D(writeData), .en(decoder_1_out10), .Q(R10_q), .clk(clk), .clr(Reset));
  Register #(.width(32)) R12 (.D(writeData), .en(decoder_1_out12), .Q(R12_q), .clk(clk), .clr(Reset));
  Register #(.width(32)) R11 (.D(writeData), .en(decoder_1_out11), .Q(R11_q), .clk(clk), .clr(Reset));
  Register #(.width(32)) R13 (.D(writeData), .en(decoder_1_out13), .Q(R13_q), .clk(clk), .clr(Reset));
  Register #(.width(32)) R14 (.D(writeData), .en(decoder_1_out14), .Q(R14_q), .clk(clk), .clr(Reset));
  Multiplexer #(.select(4), .width(32)) multiplexer_1 (
    .in0(R0_q), .in1(R1_q), .in2(R2_q), .in3(R3_q), .in4(register_1_q), .in5(R5_q), .in6(R6_q), .in7(R7_q),
    .in8(R8_q), .in9(R9_q), .in10(R10_q), .in11(R11_q), .in12(R12_q), .in13(R13_q), .in14(R14_q), .in15(R15),
    .out(RD1), .sel(A1));  // open: en
  Multiplexer #(.select(4), .width(32)) multiplexer_2 (
    .in0(R0_q), .in1(R1_q), .in2(R2_q), .in3(R3_q), .in4(register_1_q), .in5(R5_q), .in6(R6_q), .in7(R7_q),
    .in8(R8_q), .in9(R9_q), .in10(R10_q), .in11(R11_q), .in12(R12_q), .in13(R13_q), .in14(R14_q), .in15(R15),
    .out(RD2), .sel(A2));  // open: en

  // Notes on the sheet:
  //   A1,A2,-> one of 16 registers as src operands
  //   write port takes 4-bit address input A3; 32-bit write data input WD3; Write enable input WE3; and clock
  //   if the write enable is asserted, reg file writes data into specified reg on rising edge of clock
  //   a read of r15 returns the value from PC + 8 and writes to r15 must be specifically handled to update the pc bc it is separate from reg file
  //   RD1, RD2 -> take A1 and A2
  //   reads 32-bit reg vals of A1, and A2 onto RD1 and RD2
endmodule

module cpu (
  output [31:0] out_1
);

  wire ALU_FLAGS, ALU_OP, clock_1_out, control_1_alusrc, control_1_memtoreg, control_1_memwrite,
       control_1_pcsrc, control_1_regwrite;
  wire [1:0] control_1_alucontrol, control_1_immsrc, control_1_regsrc, instruction_memory_1_rd_3;
  wire [3:0] alu_conditional_1_alu_flags, instruction_memory_1_rd_4, multiplexer_2_out, multiplexer_3_out;
  wire [5:0] instruction_memory_1_rd_2;
  wire [19:0] instruction_memory_1_rd;
  wire [31:0] adder_1_out, adder_2_out, data_memory_1_rd, extend_1_extimm, multiplexer_1_out,
       multiplexer_4_out, multiplexer_5_out, PC_q, register_file_1_rd1, register_file_1_rd2;

  // Probe on ALU_FLAGS
  // Probe on ALU_OP
  // Probe on clock_1_out
  // Probe on control_1_pcsrc
  Multiplexer #(.width(32)) multiplexer_1 (
    .in0(adder_1_out), .in1(multiplexer_5_out), .out(multiplexer_1_out), .sel(control_1_pcsrc));  // open: en
  Register #(.width(32)) PC (.D(multiplexer_1_out), .Q(PC_q), .clk(clock_1_out));  // open: en, clr
  // Probe on instruction_memory_1_rd_3
  // Probe on instruction_memory_1_rd_2
  // Probe on instruction_memory_1_rd[15:12]
  // Probe on instruction_memory_1_rd_2
  // Probe on {instruction_memory_1_rd_4, instruction_memory_1_rd_3, instruction_memory_1_rd_2, instruction_memory_1_rd}
  Adder #(.width(32)) adder_1 (.a(PC_q), .b(32'h4), .out(adder_1_out));  // open: cin, cout
  // Probe on instruction_memory_1_rd_4
  // Probe on instruction_memory_1_rd_4
  instruction_memory instruction_memory_1 (
    .addr(PC_q),
    .rd({instruction_memory_1_rd_4, instruction_memory_1_rd_3, instruction_memory_1_rd_2, instruction_memory_1_rd}));
  // Probe on alu_conditional_1_alu_flags
  Adder #(.width(32)) adder_2 (.a(32'h4), .b(adder_1_out), .out(adder_2_out));  // open: cin, cout
  // Probe on {instruction_memory_1_rd_2[3:0], instruction_memory_1_rd}
  Clock clock_1 (.out(clock_1_out));
  Multiplexer #(.width(4)) multiplexer_2 (
    .in0(instruction_memory_1_rd[19:16]), .in1(4'b1111), .out(multiplexer_2_out), .sel(control_1_regsrc[0]));  // open: en
  control control_1 (
    .Cond_3_0(instruction_memory_1_rd_4), .ALUFlags3_0(alu_conditional_1_alu_flags),
    .Op(instruction_memory_1_rd_3), .Funct(instruction_memory_1_rd_2), .Rd(instruction_memory_1_rd[15:12]),
    .PCSrc(control_1_pcsrc), .RegWrite(control_1_regwrite), .MemWrite(control_1_memwrite),
    .MemtoReg(control_1_memtoreg), .ALUSrc(control_1_alusrc), .ImmSrc(control_1_immsrc),
    .RegSrc(control_1_regsrc), .ALUControl(control_1_alucontrol), .clk(clock_1_out));
  Multiplexer #(.width(4)) multiplexer_3 (
    .in0(instruction_memory_1_rd[3:0]), .in1(instruction_memory_1_rd[15:12]), .out(multiplexer_3_out),
    .sel(control_1_regsrc[1]));  // open: en
  // Probe on multiplexer_5_out
  // Probe on control_1_regwrite
  register_file register_file_1 (
    .R15(adder_2_out), .we(control_1_regwrite), .writeAddr(instruction_memory_1_rd[15:12]),
    .writeData(multiplexer_5_out), .clk(clock_1_out), .RD1(register_file_1_rd1), .A1(multiplexer_2_out),
    .RD2(register_file_1_rd2), .A2(multiplexer_3_out));  // open: Reset
  Extend extend_1 (
    .ExtImm(extend_1_extimm), ._24bits({instruction_memory_1_rd_2[3:0], instruction_memory_1_rd}),
    .ImmSrc(control_1_immsrc));
  // Probe on multiplexer_4_out
  // Probe on register_file_1_rd1
  Multiplexer #(.width(32)) multiplexer_4 (
    .in0(register_file_1_rd2), .in1(extend_1_extimm), .out(multiplexer_4_out), .sel(control_1_alusrc));  // open: en
  // Probe on register_file_1_rd2
  // Probe on extend_1_extimm
  // Probe on extend_1_extimm
  // Probe on control_1_alucontrol
  ALU_conditional alu_conditional_1 (
    .ALU_Control(control_1_alucontrol), .r(out_1), .ALU_FLAGS(alu_conditional_1_alu_flags),
    .A(register_file_1_rd1), .B(multiplexer_4_out));  // open: Zero, Negative, Carry, Overflow
  // Probe on control_1_alucontrol
  data_memory data_memory_1 (
    .address(out_1), .wd(register_file_1_rd2), .we(control_1_memwrite), .rd(data_memory_1_rd),
    .clk(clock_1_out));  // open: RESET
  // Probe on data_memory_1_rd
  Multiplexer #(.width(32)) multiplexer_5 (
    .in0(out_1), .in1(data_memory_1_rd), .out(multiplexer_5_out), .sel(control_1_memtoreg));  // open: en

  // Notes on the sheet:
  //   PCsrc
  //   PC'
  //   PC
  //   PC Plus 4
  //   CNZV
  //   RegSrc
  //   PC plus 8
  //   regWrite
  //   ALUSrc
  //   ALUControl
  //   ALUResult
  //   MemWrite
  //   ReadData
  //   MemToReg
  //   Result
endmodule

module ALU_conditional (
  input  [31:0] A,
  input  [31:0] B,
  input  [1:0] ALU_Control,
  output [31:0] r,
  output Zero,
  output [3:0] ALU_FLAGS,
  output Negative,
  output Carry,
  output Overflow
);

  wire adder_1_cout;
  wire [31:0] adder_1_out, and_1_out, or_1_out, subtractor_1_out;

  // Probe on A
  // Probe on B
  Adder #(.width(32)) adder_1 (.a(A), .b(B), .out(adder_1_out), .cout(adder_1_cout));  // open: cin
  Subtractor #(.width(32)) subtractor_1 (.a(A), .b(B), .out(subtractor_1_out));  // open: bin, bout
  assign or_1_out = A | B;  // OR_Gate or_1, 32 bits wide
  assign and_1_out = A & B;  // AND_Gate and_1, 32 bits wide
  Multiplexer #(.select(2), .width(32)) multiplexer_1 (
    .in0(adder_1_out), .in1(subtractor_1_out), .in2(or_1_out), .in3(and_1_out),
    .out({ALU_FLAGS[0], r[30:0]}), .sel(ALU_Control));  // open: en
  conditional conditional_1 (
    .ALUControl(ALU_Control), .carry(ALU_FLAGS[2]), .Overflow(ALU_FLAGS[3]), .A(A[31]), .B(B[31]),
    .C_out(adder_1_cout));
  // Probe on {ALU_FLAGS[0], r[30:0]}
  and and_2 (ALU_FLAGS[1], ~r[0], ~r[1], ~r[2], ~r[3], ~r[4], ~r[5], ~r[6], ~r[7], ~r[8], ~r[9], ~r[10], ~r[11], ~r[12], ~r[13], ~r[14], ~r[15], ~r[16], ~r[17], ~r[18], ~r[19], ~r[20], ~r[21], ~r[22], ~r[23], ~r[24], ~r[25], ~r[26], ~r[27], ~r[28], ~r[29], ~r[30], ~ALU_FLAGS[0]);  // AND_Gate

  assign Carry = ALU_FLAGS[2];
  assign Negative = ALU_FLAGS[0];
  assign Overflow = ALU_FLAGS[3];
  assign r[31] = ALU_FLAGS[0];
  assign Zero = ALU_FLAGS[1];

  // Notes on the sheet:
  //   NCZV
endmodule

module read_registers (
  input  [3:0] A1,
  input  [3:0] A2,
  output [31:0] RD1,
  output [31:0] RD2
);

  wire clock_1_out;
  wire [31:0] r0_q, r2_q, r3_q, r4_q, r5_q, r6_q, r7_q, r8_q, r9_q, r10_q, r11_q, r12_q, r13_q, r14_q, r15_q;

  Clock clock_1 (.out(clock_1_out));
  Register #(.width(32)) r0 (.Q(r0_q), .clk(clock_1_out));  // open: D, en, clr
  Register #(.width(32)) r2 (.Q(r2_q), .clk(clock_1_out));  // open: D, en, clr
  Register #(.width(32)) r4 (.Q(r4_q), .clk(clock_1_out));  // open: D, en, clr
  Register #(.width(32)) r6 (.Q(r6_q), .clk(clock_1_out));  // open: D, en, clr
  Register #(.width(32)) r8 (.Q(r8_q), .clk(clock_1_out));  // open: D, en, clr
  Register #(.width(32)) r10 (.Q(r10_q), .clk(clock_1_out));  // open: D, en, clr
  Register #(.width(32)) r12 (.Q(r12_q), .clk(clock_1_out));  // open: D, en, clr
  Register #(.width(32)) r14 (.Q(r14_q), .clk(clock_1_out));  // open: D, en, clr
  Register #(.width(32)) r1 (.Q(r0_q), .clk(clock_1_out));  // open: D, en, clr
  Register #(.width(32)) r3 (.Q(r3_q), .clk(clock_1_out));  // open: D, en, clr
  Register #(.width(32)) r5 (.Q(r5_q), .clk(clock_1_out));  // open: D, en, clr
  Register #(.width(32)) r7 (.Q(r7_q), .clk(clock_1_out));  // open: D, en, clr
  Register #(.width(32)) r9 (.Q(r9_q), .clk(clock_1_out));  // open: D, en, clr
  Register #(.width(32)) r11 (.Q(r11_q), .clk(clock_1_out));  // open: D, en, clr
  Register #(.width(32)) r13 (.Q(r13_q), .clk(clock_1_out));  // open: D, en, clr
  Register #(.width(32)) r15 (.Q(r15_q), .clk(clock_1_out));  // open: D, en, clr
  Multiplexer #(.select(4), .width(32)) multiplexer_1 (
    .in0(r0_q), .in1(r0_q), .in2(r2_q), .in3(r3_q), .in4(r4_q), .in5(r5_q), .in6(r6_q), .in7(r7_q),
    .in8(r8_q), .in9(r9_q), .in10(r10_q), .in11(r11_q), .in12(r12_q), .in13(r13_q), .in14(r14_q),
    .in15(r15_q), .out(RD1), .sel(A1));  // open: en
  Multiplexer #(.select(4), .width(32)) multiplexer_2 (
    .in0(r0_q), .in1(r0_q), .in2(r2_q), .in3(r3_q), .in4(r4_q), .in5(r5_q), .in6(r6_q), .in7(r7_q),
    .in8(r8_q), .in9(r9_q), .in10(r10_q), .in11(r11_q), .in12(r12_q), .in13(r13_q), .in14(r14_q),
    .in15(r15_q), .out(RD2), .sel(A2));  // open: en

  // Notes on the sheet:
  //   A1
  //   A2
endmodule

module write_registers (
  input  Write,
  input  [3:0] A3,
  input  [31:0] WD3
);

  wire decoder_1_out0, decoder_1_out1, decoder_1_out2, decoder_1_out3, decoder_1_out4, decoder_1_out5,
       decoder_1_out6, decoder_1_out7, decoder_1_out8, decoder_1_out9, decoder_1_out10, decoder_1_out11,
       decoder_1_out12, decoder_1_out13, decoder_1_out14, decoder_1_out15;

  Decoder #(.select(4)) decoder_1 (
    .out0(decoder_1_out0), .out1(decoder_1_out1), .out2(decoder_1_out2), .out3(decoder_1_out3),
    .out4(decoder_1_out4), .out5(decoder_1_out5), .out6(decoder_1_out6), .out7(decoder_1_out7),
    .out8(decoder_1_out8), .out9(decoder_1_out9), .out10(decoder_1_out10), .out11(decoder_1_out11),
    .out12(decoder_1_out12), .out13(decoder_1_out13), .out14(decoder_1_out14), .out15(decoder_1_out15),
    .sel(A3));  // open: en
  registers_to_write registers_to_write_1 (
    .Write(Write), .input0(decoder_1_out0), .input1(decoder_1_out1), .input2(decoder_1_out2),
    .input3(decoder_1_out3), .input4(decoder_1_out4), .input5(decoder_1_out5), .input6(decoder_1_out6),
    .input7(decoder_1_out7), .input8(decoder_1_out8), .input9(decoder_1_out9), .input10(decoder_1_out10),
    .input11(decoder_1_out11), .input12(decoder_1_out12), .input13(decoder_1_out13),
    .input14(decoder_1_out14), .input15(decoder_1_out15), .Wd3(WD3));
endmodule

module conditional (
  input  A,
  input  B,
  input  C_out,
  input  [1:0] ALUControl,
  output carry,
  output Overflow
);

  wire adder_1_out, not_1_out, xnor_1_out, xor_1_out;

  Adder #(.width(1)) adder_1 (.a(A), .b(B), .out(adder_1_out));  // open: cin, cout
  // Probe on adder_1_out
  not not_1 (not_1_out, ALUControl[1]);
  xor xor_1 (xor_1_out, adder_1_out, A);
  NotExactlyOne xnor_1 (.out(xnor_1_out), .in0(B), .in1(A), .in2(ALUControl[0]));
  and and_1 (carry, C_out, not_1_out);
  and and_2 (Overflow, not_1_out, xor_1_out, xnor_1_out);

  // Notes on the sheet:
  //   carry
  //   overflow
endmodule

module registers_to_write (
  input  Write,
  input  input0,
  input  input1,
  input  input2,
  input  input3,
  input  input4,
  input  input5,
  input  input6,
  input  input7,
  input  input8,
  input  input9,
  input  input10,
  input  input11,
  input  input12,
  input  input13,
  input  input14,
  input  input15,
  input  [31:0] Wd3
);

  wire and_1_out, and_2_out, and_3_out, and_4_out, and_5_out, and_6_out, and_7_out, and_8_out, and_9_out,
       and_10_out, and_11_out, and_12_out, and_13_out, and_14_out, and_15_out, and_16_out;

  Register #(.width(32)) r0 (.D(Wd3), .clk(and_1_out));  // open: en, Q, clr
  and and_1 (and_1_out, Write, input0);
  Register #(.width(32)) r4 (.D(Wd3), .clk(and_2_out));  // open: en, Q, clr
  and and_2 (and_2_out, Write, input4);
  Register #(.width(32)) r8 (.D(Wd3), .clk(and_3_out));  // open: en, Q, clr
  and and_3 (and_3_out, Write, input8);
  Register #(.width(32)) r12 (.D(Wd3), .clk(and_4_out));  // open: en, Q, clr
  and and_4 (and_4_out, Write, input12);
  and and_5 (and_5_out, Write, input1);
  and and_6 (and_6_out, Write, input5);
  and and_7 (and_7_out, Write, input9);
  and and_8 (and_8_out, Write, input13);
  Register #(.width(32)) r1 (.D(Wd3), .clk(and_5_out));  // open: en, Q, clr
  Register #(.width(32)) r5 (.D(Wd3), .clk(and_6_out));  // open: en, Q, clr
  Register #(.width(32)) r9 (.D(Wd3), .clk(and_7_out));  // open: en, Q, clr
  Register #(.width(32)) r13 (.D(Wd3), .clk(and_8_out));  // open: en, Q, clr
  and and_9 (and_9_out, Write, input2);
  and and_10 (and_10_out, Write, input6);
  and and_11 (and_11_out, Write, input10);
  and and_12 (and_12_out, Write, input14);
  Register #(.width(32)) r2 (.D(Wd3), .clk(and_9_out));  // open: en, Q, clr
  Register #(.width(32)) r6 (.D(Wd3), .clk(and_10_out));  // open: en, Q, clr
  Register #(.width(32)) r10 (.D(Wd3), .clk(and_11_out));  // open: en, Q, clr
  Register #(.width(32)) r14 (.D(Wd3), .clk(and_12_out));  // open: en, Q, clr
  Register #(.width(32)) r3 (.D(Wd3), .clk(and_13_out));  // open: en, Q, clr
  and and_13 (and_13_out, Write, input3);
  Register #(.width(32)) r7 (.D(Wd3), .clk(and_14_out));  // open: en, Q, clr
  and and_14 (and_14_out, Write, input7);
  Register #(.width(32)) r11 (.D(Wd3), .clk(and_15_out));  // open: en, Q, clr
  and and_15 (and_15_out, Write, input11);
  Register #(.width(32)) r15 (.D(Wd3), .clk(and_16_out));  // open: en, Q, clr
  and and_16 (and_16_out, Write, input15);
endmodule

module control (
  input  clk,
  input  [3:0] Cond_3_0,
  input  [3:0] ALUFlags3_0,
  input  [1:0] Op,
  input  [5:0] Funct,
  input  [3:0] Rd,
  output PCSrc,
  output RegWrite,
  output MemWrite,
  output MemtoReg,
  output ALUSrc,
  output [1:0] ImmSrc,
  output [1:0] RegSrc,
  output [1:0] ALUControl
);

  wire decoder_1_memwrite, decoder_1_nowrite, decoder_1_pcs, decoder_1_regwrite;
  wire [1:0] decoder_1_flagw;

  // Probe on Cond_3_0
  // Probe on ALUFlags3_0
  // Probe on Op
  // Probe on Rd
  // Probe on Funct
  decoder decoder_1 (
    .RD(Rd), .Op(Op), .Funct_5_0(Funct), .PCS(decoder_1_pcs), .RegWrite(decoder_1_regwrite),
    .MemWrite(decoder_1_memwrite), .MemToReg(MemtoReg), .ALUSrc(ALUSrc), .ImmSrc(ImmSrc), .RegSrc(RegSrc),
    .ALUControl(ALUControl), .FlagW(decoder_1_flagw), .NoWrite(decoder_1_nowrite));
  // conditional_logic conditional_logic_1: pin names not known; wires that end beside it: Cond_3_0, ALUFlags3_0, decoder_1_flagw, decoder_1_pcs, decoder_1_regwrite, decoder_1_memwrite, decoder_1_nowrite, clk, PCSrc, RegWrite, MemWrite

  // Other names for the same wires on the sheet: ALU_FLAGS[3:0] = ALUFlags3_0; ALU_OP[1:0] = Op
endmodule

module main_decoder (
  input  [1:0] Op,
  input  [5:0] Func,
  output RegWrite,
  output ALUOp,
  output MemWrite,
  output MemtoReg,
  output ALUSrc,
  output [1:0] ImmSrc,
  output [1:0] RegSrc,
  output Branch
);

  wire and_1_out, and_2_out, and_3_out, and_4_out, and_5_out, not_1_out, not_2_out, not_3_out, not_4_out;

  // Probe on Op[1]
  not not_1 (not_1_out, Op[1]);
  // Probe on Op[0]
  not not_2 (not_2_out, Op[0]);
  not not_3 (not_3_out, Func[5]);
  not not_4 (not_4_out, Func[0]);
  and and_1 (and_1_out, not_1_out, not_2_out, not_3_out);
  and and_2 (and_2_out, not_1_out, not_2_out, Func[5]);
  and and_3 (and_3_out, not_1_out, Op[0], not_4_out);
  and and_4 (and_4_out, not_1_out, Op[0], Func[0]);
  and and_5 (and_5_out, Op[1], Op[0]);
  main_decoder_output main_decoder_output_1 (
    .RegWrite(RegWrite), .ALUOp(ALUOp), .MemWrite(MemWrite), .MemtoReg(MemtoReg), .ALUSrc(ALUSrc),
    .ImmSrc(ImmSrc), .RegSrc(RegSrc), .Branch_2(Branch), .DP_Reg(and_1_out), .DP_Imm(and_2_out),
    .str(and_3_out), .ldr(and_4_out), .Branch(and_5_out));

  // Notes on the sheet:
  //   1
  //   0
  //   1
  //   0
  //   1
  //   0
  //   1
  //   0
  //   DPreg
  //   DPImm
  //   str
  //   ldr
  //   branch
endmodule

module Extend (
  input  [23:0] _24bits,
  input  [1:0] ImmSrc,
  output [31:0] ExtImm
);

  wire [31:0] n8bit_extend_1_out_2, n12bit_extend_1_out_2, n24bit_extend_1_out_2;

  _8bit_extend u_8bit_extend_1 (.out_2(n8bit_extend_1_out_2), .in_1(_24bits));
  _12bit_extend u_12bit_extend_1 (.out_2(n12bit_extend_1_out_2), .in_1(_24bits));
  _24bit_extend u_24bit_extend_1 (.out_2(n24bit_extend_1_out_2), .in_1(_24bits));
  Multiplexer #(.select(2), .width(32)) multiplexer_1 (
    .in0(n8bit_extend_1_out_2), .in1(n12bit_extend_1_out_2), .in2(n24bit_extend_1_out_2), .out(ExtImm),
    .sel(ImmSrc));  // open: in3, en
endmodule

module _8bit_extend (
  input  [23:0] in_1,
  output [31:0] out_2
);

  assign out_2 = {{24{1'b0}}, in_1[7:0]};  // Bit_Extender bit_extender_1
endmodule

module _12bit_extend (
  input  [23:0] in_1,
  output [31:0] out_2
);

  assign out_2 = {{20{1'b0}}, in_1[11:0]};  // Bit_Extender bit_extender_1
endmodule

module _24bit_extend (
  input  [23:0] in_1,
  output [31:0] out_2
);

  assign out_2 = {{8{in_1[23]}}, in_1};  // Bit_Extender bit_extender_1
endmodule

module conditional_logic (
  input  PCS,
  input  RegW,
  input  NoWrite,
  input  MemW,
  input  [1:0] FlagW,
  input  [3:0] Cond,
  input  [3:0] ALUFlags,
  input  clk,
  output PCSrc,
  output RegWrite,
  output MemWrite
);

  wire cond_check_1_condex;
  wire [1:0] and_1_out, bit_extender_1_out, register_1_q, register_2_q;

  Register #(.width(2)) register_1 (.D(ALUFlags[3:2]), .Q(register_1_q), .clk(clk), .clr(and_1_out[0]));  // open: en
  Register #(.width(2)) register_2 (.D(ALUFlags[1:0]), .Q(register_2_q), .clk(clk), .clr(and_1_out[1]));  // open: en
  assign and_1_out = FlagW & bit_extender_1_out;  // AND_Gate and_1, 2 bits wide
  assign bit_extender_1_out = {{1{1'b0}}, cond_check_1_condex};  // Bit_Extender bit_extender_1
  cond_check cond_check_1 (.Flags3_2(register_1_q), .Flags1_0(register_2_q), .CondEx(cond_check_1_condex), .Cond(Cond));
  and and_2 (PCSrc, PCS, cond_check_1_condex);
  and and_3 (RegWrite, RegW, ~NoWrite, cond_check_1_condex);  // AND_Gate
  and and_4 (MemWrite, MemW, cond_check_1_condex);
  // Probe on cond_check_1_condex

  // Notes on the sheet:
  //   CondEx
endmodule

module decoder (
  input  [3:0] RD,
  input  [1:0] Op,
  input  [5:0] Funct_5_0,
  output PCS,
  output RegWrite,
  output MemWrite,
  output MemToReg,
  output ALUSrc,
  output [1:0] ImmSrc,
  output [1:0] RegSrc,
  output [1:0] ALUControl,
  output NoWrite,
  output [1:0] FlagW
);

  wire main_decoder_1_aluop, main_decoder_1_branch;

  // Probe on main_decoder_1_aluop
  // Probe on Funct_5_0[4:0]
  // Probe on Funct_5_0[4:0]
  PC_logic pc_logic_1 (.Rd_3_0(RD), .RegWrite(RegWrite), .PCS(PCS), .Branch(main_decoder_1_branch));
  main_decoder main_decoder_1 (
    .Op(Op), .Func(Funct_5_0), .RegWrite(RegWrite), .ALUOp(main_decoder_1_aluop), .MemWrite(MemWrite),
    .MemtoReg(MemToReg), .ALUSrc(ALUSrc), .ImmSrc(ImmSrc), .RegSrc(RegSrc), .Branch(main_decoder_1_branch));
  ALU_decoder ALUOp (
    .Funct(Funct_5_0[4:0]), .ALUControl(ALUControl), .FlagW(FlagW), .ALUOp(main_decoder_1_aluop),
    .NoWrite(NoWrite));

  // Notes on the sheet:
  //   ALUOp
  //   FlagW0 = 1 ->CV(Flags1:0) are saved 
  //   FlagW1  = 1 -> NZ(Flags3:2) are saved
endmodule

module ALU_decoder (
  input  ALUOp,
  input  [4:0] Funct,
  output [1:0] ALUControl,
  output NoWrite,
  output [1:0] FlagW
);

  wire [1:0] set_control_1_alucontrol;

  // Probe on Funct
  // Probe on Funct
  // Probe on Funct[4:1]
  // Probe on Funct[0]
  set_Control set_control_1 (
    .ALUControl(set_control_1_alucontrol), .FlagW(FlagW), .funct4_0(Funct[4:1]), .Funct0(Funct[0]),
    .NoWrite(NoWrite));
  Multiplexer #(.width(2)) multiplexer_1 (
    .in0(2'b00), .in1(set_control_1_alucontrol), .out(ALUControl), .sel(ALUOp));  // open: en
endmodule

module PC_logic (
  input  [3:0] Rd_3_0,
  input  RegWrite,
  input  Branch,
  output PCS
);

  wire and_1_out, and_2_out, and_3_out, and_4_out;

  and and_1 (and_1_out, Rd_3_0[0], Rd_3_0[1], Rd_3_0[2], Rd_3_0[3]);
  and and_2 (and_2_out, and_1_out, 1'b1);
  and and_3 (and_3_out, RegWrite, 1'b1);
  // Probe on and_2_out
  // Probe on and_3_out
  and and_4 (and_4_out, and_2_out, and_3_out);
  or or_1 (PCS, and_4_out, Branch);
endmodule

module set_Control (
  input  [3:0] funct4_0,
  input  Funct0,
  output NoWrite,
  output [1:0] ALUControl,
  output [1:0] FlagW
);

  wire [1:0] get_flagw_1_flagw;

  Multiplexer #(.select(4), .width(2)) multiplexer_1 (
    .in0(2'b10), .in2(2'b01), .in4(2'b00), .in5(2'b00), .in10(2'b01), .in12(2'b11), .out(ALUControl),
    .sel(funct4_0));  // open: in1, in3, in6, in7, in8, in9, in11, in13, in14, in15, en
  // Probe on funct4_0
  get_FlagW get_flagw_1 (.FlagW(get_flagw_1_flagw), .ALUControl1(ALUControl));
  Multiplexer #(.select(4)) multiplexer_2 (
    .in0(1'b0), .in1(1'b0), .in2(1'b0), .in3(1'b0), .in4(1'b0), .in5(1'b0), .in6(1'b0), .in7(1'b0),
    .in8(1'b0), .in9(1'b0), .in10(1'b1), .in11(1'b0), .in12(1'b0), .in13(1'b0), .in14(1'b0), .in15(1'b0),
    .out(NoWrite), .sel(funct4_0));  // open: en
  Multiplexer #(.width(2)) multiplexer_3 (.in0(2'b00), .in1(get_flagw_1_flagw), .out(FlagW), .sel(Funct0));  // open: en
endmodule

module get_FlagW (
  input  [1:0] ALUControl1,
  output [1:0] FlagW
);

  wire and_1_out;

  not not_1 (FlagW[0], and_1_out);
  and and_1 (and_1_out, ALUControl1[1], 1'b1);

  assign FlagW[1] = 1'b1;
endmodule

module main_decoder_output (
  input  DP_Reg,
  input  DP_Imm,
  input  str,
  input  ldr,
  input  Branch,
  output RegWrite,
  output ALUOp,
  output MemWrite,
  output MemtoReg,
  output ALUSrc,
  output [1:0] ImmSrc,
  output [1:0] RegSrc,
  output Branch_2
);

  or or_1 (RegWrite, DP_Reg, ldr, DP_Imm);
  or or_2 (ALUOp, DP_Reg, DP_Imm);
  or or_3 (ALUSrc, DP_Imm, str, ldr, Branch);
  or or_4 (ImmSrc[0], str, ldr);
  nor nor_1 (ImmSrc[1], DP_Imm, str, ldr);

  assign Branch_2 = Branch;
  assign MemtoReg = ldr;
  assign MemWrite = str;
  assign RegSrc = {str, Branch};
endmodule

module cond_check (
  input  [1:0] Flags3_2,
  input  [3:0] Cond,
  input  [1:0] Flags1_0,
  output CondEx
);

  wire and_1_out, not_1_out, not_2_out, xor_1_out;

  not not_1 (not_1_out, Flags3_2[0]);
  xor xor_1 (xor_1_out, Flags3_2[1], Flags1_0[0]);
  and and_1 (and_1_out, not_1_out, not_2_out);
  not not_2 (not_2_out, xor_1_out);
  Multiplexer #(.select(4)) multiplexer_1 (
    .in0(Flags3_2[0]), .in1(not_1_out), .in12(and_1_out), .in14(1'b1), .out(CondEx), .sel(Cond));  // open: in2, in3, in4, in5, in6, in7, in8, in9, in10, in11, in13, in15, en

  // Notes on the sheet:
  //   Z
  //   N
  //   V
  //   C
  //   eq
  //   ne
  //   gt
  //   eq
endmodule

module registers (
  input  [31:0] R15,
  input  we,
  input  [3:0] writeAddr,
  input  [31:0] writeData,
  input  clk,
  input  Reset,
  input  [3:0] A1,
  input  [3:0] A2,
  output [31:0] RD1,
  output [31:0] RD2
);

  wire decoder_1_out0, decoder_1_out1, decoder_1_out2, decoder_1_out3, decoder_1_out4, decoder_1_out5,
       decoder_1_out6, decoder_1_out7, decoder_1_out8, decoder_1_out9, decoder_1_out10, decoder_1_out11,
       decoder_1_out12, decoder_1_out13, decoder_1_out14;
  wire [31:0] R0_q, R1_q, R2_q, R3_q, R5_q, R6_q, R7_q, R8_q, R9_q, R10_q, R11_q, R12_q, R13_q, R14_q,
       register_1_q;

  Decoder #(.select(4)) decoder_1 (
    .out0(decoder_1_out0), .out1(decoder_1_out1), .out2(decoder_1_out2), .out3(decoder_1_out3),
    .out4(decoder_1_out4), .out5(decoder_1_out5), .out6(decoder_1_out6), .out7(decoder_1_out7),
    .out8(decoder_1_out8), .out9(decoder_1_out9), .out10(decoder_1_out10), .out11(decoder_1_out11),
    .out12(decoder_1_out12), .out13(decoder_1_out13), .out14(decoder_1_out14), .sel(writeAddr), .en(we));  // open: out15
  Register #(.width(32)) R0 (.D(writeData), .en(decoder_1_out0), .Q(R0_q), .clk(clk), .clr(Reset));
  Register #(.width(32)) R1 (.D(writeData), .en(decoder_1_out1), .Q(R1_q), .clk(clk), .clr(Reset));
  Register #(.width(32)) R2 (.D(writeData), .en(decoder_1_out2), .Q(R2_q), .clk(clk), .clr(Reset));
  Register #(.width(32)) register_1 (.D(writeData), .en(decoder_1_out4), .Q(register_1_q), .clk(clk), .clr(Reset));
  Register #(.width(32)) R3 (.D(writeData), .en(decoder_1_out3), .Q(R3_q), .clk(clk), .clr(Reset));
  Register #(.width(32)) R5 (.D(writeData), .en(decoder_1_out5), .Q(R5_q), .clk(clk), .clr(Reset));
  Register #(.width(32)) R6 (.D(writeData), .en(decoder_1_out6), .Q(R6_q), .clk(clk), .clr(Reset));
  Register #(.width(32)) R7 (.D(writeData), .en(decoder_1_out7), .Q(R7_q), .clk(clk), .clr(Reset));
  Register #(.width(32)) R8 (.D(writeData), .en(decoder_1_out8), .Q(R8_q), .clk(clk), .clr(Reset));
  Register #(.width(32)) R9 (.D(writeData), .en(decoder_1_out9), .Q(R9_q), .clk(clk), .clr(Reset));
  Register #(.width(32)) R10 (.D(writeData), .en(decoder_1_out10), .Q(R10_q), .clk(clk), .clr(Reset));
  Register #(.width(32)) R12 (.D(writeData), .en(decoder_1_out12), .Q(R12_q), .clk(clk), .clr(Reset));
  Register #(.width(32)) R11 (.D(writeData), .en(decoder_1_out11), .Q(R11_q), .clk(clk), .clr(Reset));
  Register #(.width(32)) R13 (.D(writeData), .en(decoder_1_out13), .Q(R13_q), .clk(clk), .clr(Reset));
  Register #(.width(32)) R14 (.D(writeData), .en(decoder_1_out14), .Q(R14_q), .clk(clk), .clr(Reset));
  Multiplexer #(.select(4), .width(32)) multiplexer_1 (
    .in0(R0_q), .in1(R1_q), .in2(R2_q), .in3(R3_q), .in4(register_1_q), .in5(R5_q), .in6(R6_q), .in7(R7_q),
    .in8(R8_q), .in9(R9_q), .in10(R10_q), .in11(R11_q), .in12(R12_q), .in13(R13_q), .in14(R14_q), .in15(R15),
    .out(RD1), .sel(A1));  // open: en
  Multiplexer #(.select(4), .width(32)) multiplexer_2 (
    .in0(R0_q), .in1(R1_q), .in2(R2_q), .in3(R3_q), .in4(register_1_q), .in5(R5_q), .in6(R6_q), .in7(R7_q),
    .in8(R8_q), .in9(R9_q), .in10(R10_q), .in11(R11_q), .in12(R12_q), .in13(R13_q), .in14(R14_q), .in15(R15),
    .out(RD2), .sel(A2));  // open: en
endmodule

module ALU_dec2 (
  input  ALUOp,
  input  Funct4,
  input  Funct3,
  input  Funct2,
  input  Funct1,
  input  Funct0,
  output [1:0] ALUcontrol,
  output [1:0] FlagW
);

  wire and_1_out, and_2_out;

  and and_1 (and_1_out, ALUOp, Funct4, ~Funct3, Funct2, ~Funct1, Funct0);  // AND_Gate
  and and_2 (and_2_out, ALUOp, ~Funct4, Funct3, ~Funct2, ~Funct1, Funct0);  // AND_Gate
  or or_1 (FlagW[0], and_1_out, and_2_out);

  assign ALUcontrol = 2'b00;
  assign FlagW[1] = 1'b0;
endmodule
